# Fritzing sketch mcp3008 (saved by Fritzing 0.9.3b)
breadboards: 2

parts:
  Pico1 = Raspberry Pi Pico
  ADC1 = MCP3008 [package=dil16]
  R1 = Rotary Potentiometer (Small) [maximum_resistance=100kΩ package=THT]

nets:
  N1: Pico1.GND, ADC1.DGND, R1.leg1
  3V3: Pico1.3V3, ADC1.VREF, ADC1.VDD, R1.leg2
  N2: Pico1.GP22, ADC1.CS/SHDN
  N3: Pico1.GP4, ADC1.Dout
  N4: Pico1.GP3, ADC1.Din
  N5: Pico1.GP2, ADC1.CLK
  N6: ADC1.CH0, R1.wiper

custom parts:
  Raspberry Pi Pico: Raspberry Pi Pico. Based around the RP2040 microcontroller the Pico is a low cost microcontroller device bringing Raspberry Pi quality, cost, and easy of use to the microcontroller space.
